# Fritzing sketch B27_Schematics (saved by Fritzing 0.9.9b)
breadboards: 2

parts:
  Part1 = Arduino Uno (Rev3) - ICSP
  R5 = Resistor [tolerance=±5% resistance=220 package="0603 [SMD]"]
  LED1 = LED - 5mm [color="Red (633nm)" current=0.030 package="5 mm [THT]"]
  J1 = Piezo Speaker
  R7 = Resistor [tolerance=±5% resistance=1k package="0603 [SMD]"]
  PIR1 = PIR sensor

nets:
  N1: Part1.D8, PIR1.SIG
  N2: Part1.D6_PWM, LED1.anode
  N3: Part1.D7, R7.Pin_1
  5V: Part1.5V, PIR1.VDD
  GND: Part1.GND, R5.Pin_1, J1.pin1, PIR1.GND
  N4: R5.Pin_0, LED1.cathode
  N5: J1.pin2, R7.Pin_0
